# Fritzing sketch push_button_led_log (saved by Fritzing 0.9.3b)
breadboards: 1

parts:
  Part1 = Arduino Mega 2560 (Rev3)
  S1 = Pushbutton [package="[THT]"]
  R1 = Resistor [tolerance=±5% resistance=220 package=THT]
  LED1 = LED - 5mm [color="White (4500K)" package="5 mm [THT]"]

nets:
  N1: Part1.GND, S1.Pin_1, S1.Pin_2, LED1.anode
  N2: Part1.D13_PWM, LED1.cathode
  N3: Part1.5V, R1.Pin_1
  N4: Part1.D22, S1.Pin_3, S1.Pin_4, R1.Pin_0
